# Fritzing sketch Sketch (saved by Fritzing 0.9.2b)

parts:
  Composant1 = Arduino Uno (Rev3)
  LED1 = RGB LED (com. cathode, rbg) [package="5 mm [THT]"]

nets:
  N1: Composant1.GND, LED1.common_cathode
  N2: Composant1.D3_PWM, LED1.red_anode
  N3: Composant1.D5_PWM, LED1.blue_anode
  N4: Composant1.D6_PWM, LED1.green_anode
